# Fritzing sketch emoticon-robot (saved by Fritzing 0.9.0b)
breadboards: 1

parts:
  부품1 = Arduino Uno (Rev3)
  LCD1 = LCD screen
  R1 = Resistor [tolerance=±5% resistance=1k package=THT]  # not connected
  부품2 = Bluetooth Mate Silver

nets:
  N1: 부품1.D11_PWM/MOSI, LCD1.E
  N2: 부품1.D12/MISO, LCD1.RS
  N3: 부품1.D0/RX, 부품2.TX_5V
  N4: 부품1.D1/TX, 부품2.RX_5V
  N5: 부품1.D2, LCD1.DB4
  N6: 부품1.D3_PWM, LCD1.DB5
  N7: 부품1.D4, LCD1.DB6
  N8: 부품1.D5_PWM, LCD1.DB7
  3V3: 부품1.3V3, LCD1.VSS, LCD1.R/W, 부품2.CTS_5V
  5V: 부품1.5V, LCD1.VDD, 부품2.VCC
